// Logisim project adders.circ as structural Verilog: 3 circuits, main circuit main
module main (
  input  [7:0] x1,
  input  [7:0] x2,
  output [7:0] s,
  output co
);

  wire full_adder_1_co, full_adder_2_co, full_adder_3_co, full_adder_4_co, full_adder_5_co, full_adder_6_co,
       half_adder_1_co;

  half_adder half_adder_1 (.x1(x1[0]), .x2(x2[0]), .co(half_adder_1_co), .s(s[0]));
  full_adder full_adder_1 (.x1(x1[1]), .x2(x2[1]), .ci(half_adder_1_co), .s(s[1]), .co(full_adder_1_co));
  full_adder full_adder_2 (.x1(x1[2]), .x2(x2[2]), .ci(full_adder_1_co), .s(s[2]), .co(full_adder_2_co));
  full_adder full_adder_3 (.x1(x1[3]), .x2(x2[3]), .ci(full_adder_2_co), .s(s[3]), .co(full_adder_3_co));
  full_adder full_adder_4 (.x1(x1[4]), .x2(x2[4]), .ci(full_adder_3_co), .s(s[4]), .co(full_adder_4_co));
  full_adder full_adder_5 (.x1(x1[5]), .x2(x2[5]), .ci(full_adder_4_co), .s(s[5]), .co(full_adder_5_co));
  full_adder full_adder_6 (.x1(x1[6]), .x2(x2[6]), .ci(full_adder_5_co), .s(s[6]), .co(full_adder_6_co));
  full_adder full_adder_7 (.x1(x1[7]), .x2(x2[7]), .ci(full_adder_6_co), .s(s[7]), .co(co));

  // Notes on the sheet:
  //   Lab: Logisim Adders
endmodule

module half_adder (
  input  x1,
  input  x2,
  output co,
  output s
);

  xor xor_1 (s, x1, x2);
  and and_1 (co, x1, x2);
endmodule

module full_adder (
  input  x1,
  input  x2,
  input  ci,
  output co,
  output s
);

  wire half_adder_1_co, half_adder_1_s, half_adder_2_co;

  half_adder half_adder_1 (.x1(x1), .x2(x2), .co(half_adder_1_co), .s(half_adder_1_s));
  half_adder half_adder_2 (.x1(half_adder_1_s), .x2(ci), .co(half_adder_2_co), .s(s));
  or or_1 (co, half_adder_1_co, half_adder_2_co);
endmodule
