// Logisim project 4-bit-alu.circ as structural Verilog: 2 circuits, main circuit 4-bit ALU
// 1b ALU
module _1_bit_ALU (
  input  [1:0] operation,
  input  a_invert,
  input  b_invert,
  input  c_in,
  input  a,
  input  b,
  output result,
  output c_out
);

  wire adder_1_out, and_1_out, multiplexer_1_out, multiplexer_2_out, not_1_out, not_2_out, or_1_out;

  not not_1 (not_1_out, a);
  not not_2 (not_2_out, b);
  Multiplexer #(.enable("false")) multiplexer_1 (.in0(a), .in1(not_1_out), .out(multiplexer_1_out), .sel(a_invert));
  Multiplexer #(.enable("false")) multiplexer_2 (.in0(b), .in1(not_2_out), .out(multiplexer_2_out), .sel(b_invert));
  and and_1 (and_1_out, multiplexer_1_out, multiplexer_2_out);
  or or_1 (or_1_out, multiplexer_1_out, multiplexer_2_out);
  Adder #(.width(1)) adder_1 (
    .a(multiplexer_1_out), .b(multiplexer_2_out), .out(adder_1_out), .cin(c_in), .cout(c_out));
  Multiplexer #(.select(2), .enable("false")) multiplexer_3 (
    .in0(and_1_out), .in1(or_1_out), .in2(adder_1_out), .out(result), .sel(operation));  // open: in3

  // Notes on the sheet:
  //   Assignment: Logisim ALU
endmodule

// 4b ALU
module _4_bit_ALU (
  input  b_invert,
  input  c_in,
  input  a_invert,
  input  [1:0] operation,
  input  [3:0] a,
  input  [3:0] b,
  output [3:0] result,
  output c_out
);

  wire n1_bit_alu_1_c_out, n1_bit_alu_2_c_out, n1_bit_alu_3_c_out;

  _1_bit_ALU u_1_bit_alu_1 (
    .a(a[0]), .b(b[0]), .result(result[0]), .a_invert(a_invert), .b_invert(b_invert), .c_in(c_in),
    .operation(operation), .c_out(n1_bit_alu_1_c_out));
  _1_bit_ALU u_1_bit_alu_2 (
    .a(a[1]), .b(b[1]), .result(result[1]), .a_invert(a_invert), .b_invert(b_invert),
    .c_in(n1_bit_alu_1_c_out), .operation(operation), .c_out(n1_bit_alu_2_c_out));
  _1_bit_ALU u_1_bit_alu_3 (
    .a(a[2]), .b(b[2]), .result(result[2]), .a_invert(a_invert), .b_invert(b_invert),
    .c_in(n1_bit_alu_2_c_out), .operation(operation), .c_out(n1_bit_alu_3_c_out));
  _1_bit_ALU u_1_bit_alu_4 (
    .a(a[3]), .b(b[3]), .result(result[3]), .a_invert(a_invert), .b_invert(b_invert),
    .c_in(n1_bit_alu_3_c_out), .operation(operation), .c_out(c_out));

  // Notes on the sheet:
  //   Assignment: Logisim ALU
endmodule
