// Logisim project complete-4-bit-alu.circ as structural Verilog: 4 circuits, main circuit 4-bit ALU
// 1b ALU
module _1_bit_ALU (
  input  [1:0] operation,
  input  a_invert,
  input  b_invert,
  input  c_in,
  input  a,
  input  b,
  input  less,
  output result,
  output c_out
);

  wire adder_1_out, and_1_out, multiplexer_1_out, multiplexer_2_out, not_1_out, not_2_out, or_1_out;

  not not_1 (not_1_out, a);
  not not_2 (not_2_out, b);
  Multiplexer #(.enable("false")) multiplexer_1 (.in0(a), .in1(not_1_out), .out(multiplexer_1_out), .sel(a_invert));
  Multiplexer #(.enable("false")) multiplexer_2 (.in0(b), .in1(not_2_out), .out(multiplexer_2_out), .sel(b_invert));
  and and_1 (and_1_out, multiplexer_1_out, multiplexer_2_out);
  or or_1 (or_1_out, multiplexer_1_out, multiplexer_2_out);
  Adder #(.width(1)) adder_1 (
    .a(multiplexer_1_out), .b(multiplexer_2_out), .out(adder_1_out), .cin(c_in), .cout(c_out));
  Multiplexer #(.select(2), .enable("false")) multiplexer_3 (
    .in0(and_1_out), .in1(or_1_out), .in2(adder_1_out), .in3(less), .out(result), .sel(operation));

  // Notes on the sheet:
  //   Assignment: Logisim ALU
endmodule

// 4b ALU
module _4_bit_ALU (
  input  b_invert,
  input  c_in,
  input  a_invert,
  input  [1:0] operation,
  input  [3:0] a,
  input  [3:0] b,
  output [3:0] result,
  output c_out,
  output overflow
);

  wire msb_alu_1_set, n1_bit_alu_1_c_out, n1_bit_alu_2_c_out, n1_bit_alu_3_c_out, xor_1_out;

  xor xor_1 (xor_1_out, overflow, msb_alu_1_set);
  overflow_detector overflow_detector_1 (
    .b_invert(b_invert), .a(a[3]), .b(b[3]), .sum(msb_alu_1_set), .overflow(overflow));
  _1_bit_ALU u_1_bit_alu_1 (
    .a(a[0]), .b(b[0]), .result(result[0]), .a_invert(a_invert), .b_invert(b_invert), .c_in(c_in),
    .operation(operation), .c_out(n1_bit_alu_1_c_out), .less(xor_1_out));
  _1_bit_ALU u_1_bit_alu_2 (
    .a(a[1]), .b(b[1]), .result(result[1]), .a_invert(a_invert), .b_invert(b_invert),
    .c_in(n1_bit_alu_1_c_out), .operation(operation), .c_out(n1_bit_alu_2_c_out), .less(1'b0));
  _1_bit_ALU u_1_bit_alu_3 (
    .a(a[2]), .b(b[2]), .result(result[2]), .a_invert(a_invert), .b_invert(b_invert),
    .c_in(n1_bit_alu_2_c_out), .operation(operation), .c_out(n1_bit_alu_3_c_out), .less(1'b0));
  MSB_ALU msb_alu_1 (
    .a(a[3]), .b(b[3]), .less(1'b0), .a_invert(a_invert), .b_invert(b_invert), .c_in(n1_bit_alu_3_c_out),
    .operation(operation), .c_out(c_out), .result(result[3]), .set(msb_alu_1_set));

  // Notes on the sheet:
  //   Assignment: Logisim ALU
endmodule

module MSB_ALU (
  input  [1:0] operation,
  input  a_invert,
  input  b_invert,
  input  c_in,
  input  a,
  input  b,
  input  less,
  output result,
  output set,
  output c_out
);

  wire and_1_out, multiplexer_1_out, multiplexer_2_out, not_1_out, not_2_out, or_1_out;

  not not_1 (not_1_out, a);
  not not_2 (not_2_out, b);
  Multiplexer #(.enable("false")) multiplexer_1 (.in0(a), .in1(not_1_out), .out(multiplexer_1_out), .sel(a_invert));
  Multiplexer #(.enable("false")) multiplexer_2 (.in0(b), .in1(not_2_out), .out(multiplexer_2_out), .sel(b_invert));
  and and_1 (and_1_out, multiplexer_1_out, multiplexer_2_out);
  or or_1 (or_1_out, multiplexer_1_out, multiplexer_2_out);
  Adder #(.width(1)) adder_1 (.a(multiplexer_1_out), .b(multiplexer_2_out), .out(set), .cin(c_in), .cout(c_out));
  Multiplexer #(.select(2), .enable("false")) multiplexer_3 (
    .in0(and_1_out), .in1(or_1_out), .in2(set), .in3(less), .out(result), .sel(operation));

  // Notes on the sheet:
  //   Assignment: Logisim ALU
endmodule

module overflow_detector (
  input  b_invert,
  input  a,
  input  b,
  input  sum,
  output overflow
);

  wire and_1_out, and_2_out, and_3_out, and_4_out, not_1_out, not_2_out, not_3_out, not_4_out;

  not not_1 (not_1_out, b_invert);
  not not_2 (not_2_out, a);
  not not_3 (not_3_out, b);
  not not_4 (not_4_out, sum);
  and and_1 (and_1_out, not_1_out, not_2_out, not_3_out, sum);
  and and_2 (and_2_out, not_1_out, a, b, not_4_out);
  and and_3 (and_3_out, b_invert, not_2_out, b, sum);
  and and_4 (and_4_out, b_invert, a, not_3_out, not_4_out);
  or or_1 (overflow, and_4_out, and_3_out, and_2_out, and_1_out);

  // Notes on the sheet:
  //   Assignment: Logisim ALU
endmodule
