// Logisim project registers.circ as structural Verilog: 3 circuits, main circuit main
module main (
);


  // Notes on the sheet:
  //   Assignment: Logisim Register File
endmodule

module _4_bit_register (
  input  clock,
  input  write_enable,
  input  [3:0] data,
  output [3:0] \output 
);

  D_Flip_Flop #(.trigger("falling")) d_ff_1 (
    .clk(clock), .D(data[0]), .Q(\output [0]), .en(write_enable));  // open: Qn, preset, reset
  D_Flip_Flop #(.trigger("falling")) d_ff_2 (
    .clk(clock), .D(data[1]), .Q(\output [1]), .en(write_enable));  // open: Qn, preset, reset
  D_Flip_Flop #(.trigger("falling")) d_ff_3 (
    .clk(clock), .D(data[2]), .Q(\output [2]), .en(write_enable));  // open: Qn, preset, reset
  D_Flip_Flop #(.trigger("falling")) d_ff_4 (
    .clk(clock), .D(data[3]), .Q(\output [3]), .en(write_enable));  // open: Qn, preset, reset

  // Notes on the sheet:
  //   Assignment: Logisim Register File
endmodule

module _4x4_register (
  input  [1:0] read,
  input  [1:0] write,
  input  write_enable,
  input  clock,
  input  [3:0] data,
  output [3:0] \output 
);

  wire and_1_out, and_2_out, and_3_out, and_4_out, decoder_1_out0, decoder_1_out1, decoder_1_out2,
       decoder_1_out3;
  wire [3:0] n4_bit_register_1_output, n4_bit_register_2_output, n4_bit_register_3_output,
       n4_bit_register_4_output;

  Decoder #(.select(2), .enable("false")) decoder_1 (
    .out0(decoder_1_out0), .out1(decoder_1_out1), .out2(decoder_1_out2), .out3(decoder_1_out3), .sel(write));
  and and_1 (and_1_out, write_enable, decoder_1_out0);
  and and_2 (and_2_out, decoder_1_out1, write_enable);
  and and_3 (and_3_out, write_enable, decoder_1_out2);
  and and_4 (and_4_out, write_enable, decoder_1_out3);
  _4_bit_register u_4_bit_register_1 (
    .write_enable(and_1_out), .clock(clock), .data(data), .\output (n4_bit_register_1_output));
  _4_bit_register u_4_bit_register_2 (
    .write_enable(and_2_out), .clock(clock), .data(data), .\output (n4_bit_register_2_output));
  _4_bit_register u_4_bit_register_3 (
    .write_enable(and_3_out), .clock(clock), .data(data), .\output (n4_bit_register_3_output));
  _4_bit_register u_4_bit_register_4 (
    .write_enable(and_4_out), .clock(clock), .data(data), .\output (n4_bit_register_4_output));
  Multiplexer #(.select(2), .width(4), .enable("false")) multiplexer_1 (
    .in0(n4_bit_register_1_output), .in1(n4_bit_register_2_output), .in2(n4_bit_register_3_output),
    .in3(n4_bit_register_4_output), .out(\output ), .sel(read));

  // Notes on the sheet:
  //   Assignment: Logisim Register File
endmodule
