// Logisim project MiniLab Circuits.circ as structural Verilog: 4 circuits, main circuit main
module main (
  input  in_1,
  input  in_2,
  input  in_3,
  input  in_4,
  output out_5,
  output out_6
);

  wire and_1_out, and_2_out, and_3_out;

  and and_1 (and_1_out, ~in_4, ~in_2);  // AND_Gate
  and and_2 (and_2_out, in_3, ~in_2);  // AND_Gate
  and and_3 (and_3_out, ~in_4, in_3);  // AND_Gate
  or or_1 (out_6, and_3_out, and_2_out, and_1_out);

  assign out_5 = in_1;
endmodule

module _3_bit_decoder (
  input  [2:0] _3_bit_Input,
  output Out0,
  output Out1,
  output Out2,
  output Out3,
  output Out4,
  output Out5,
  output Out6,
  output Out7
);

  and and_1 (Out0, ~_3_bit_Input[0], ~_3_bit_Input[1], ~_3_bit_Input[2]);  // AND_Gate
  and and_2 (Out1, ~_3_bit_Input[2], ~_3_bit_Input[1], _3_bit_Input[0]);  // AND_Gate
  and and_3 (Out2, ~_3_bit_Input[2], _3_bit_Input[1], ~_3_bit_Input[0]);  // AND_Gate
  and and_4 (Out3, ~_3_bit_Input[2], _3_bit_Input[1], _3_bit_Input[0]);  // AND_Gate
  and and_5 (Out4, _3_bit_Input[2], ~_3_bit_Input[1], ~_3_bit_Input[0]);  // AND_Gate
  and and_6 (Out5, _3_bit_Input[2], ~_3_bit_Input[1], _3_bit_Input[0]);  // AND_Gate
  and and_7 (Out6, _3_bit_Input[2], _3_bit_Input[1], ~_3_bit_Input[0]);  // AND_Gate
  and and_8 (Out7, _3_bit_Input[2], _3_bit_Input[1], _3_bit_Input[0]);
endmodule

module _4_input_MUX (
  input  in_1,
  input  [1:0] in_2,
  input  in_3,
  input  in_4,
  input  in_5,
  output out_6
);

  wire and_1_out, and_2_out, and_3_out, and_4_out, and_5_out, and_6_out, and_7_out, and_8_out;

  and and_1 (and_1_out, ~in_2[0], ~in_2[1]);  // AND_Gate
  and and_2 (and_2_out, in_2[0], ~in_2[1]);  // AND_Gate
  and and_3 (and_3_out, ~in_2[0], in_2[1]);  // AND_Gate
  and and_4 (and_4_out, in_2[0], in_2[1]);
  and and_5 (and_5_out, in_1, and_1_out);
  and and_6 (and_6_out, in_3, and_2_out);
  and and_7 (and_7_out, and_3_out, in_4);
  and and_8 (and_8_out, and_4_out, in_5);
  or or_1 (out_6, and_5_out, and_6_out, and_7_out, and_8_out);
endmodule

module _8_input_MUX (
  input  in_1,
  input  [2:0] in_2,
  input  in_3,
  input  in_4,
  input  in_5,
  input  in_6,
  input  in_7,
  input  in_8,
  input  in_9,
  output out_10
);

  wire and_1_out, and_2_out, and_3_out, and_4_out, and_5_out, and_6_out, and_7_out, and_8_out,
       n3_bit_decoder_1_out0, n3_bit_decoder_1_out1, n3_bit_decoder_1_out2, n3_bit_decoder_1_out3,
       n3_bit_decoder_1_out4, n3_bit_decoder_1_out5, n3_bit_decoder_1_out6, n3_bit_decoder_1_out7, or_1_out,
       or_2_out;

  _3_bit_decoder u_3_bit_decoder_1 (
    ._3_bit_Input(in_2), .Out0(n3_bit_decoder_1_out0), .Out1(n3_bit_decoder_1_out1),
    .Out2(n3_bit_decoder_1_out2), .Out3(n3_bit_decoder_1_out3), .Out4(n3_bit_decoder_1_out4),
    .Out5(n3_bit_decoder_1_out5), .Out6(n3_bit_decoder_1_out6), .Out7(n3_bit_decoder_1_out7));
  and and_1 (and_1_out, n3_bit_decoder_1_out0, in_1);
  and and_2 (and_2_out, n3_bit_decoder_1_out1, in_3);
  and and_3 (and_3_out, n3_bit_decoder_1_out2, in_4);
  and and_4 (and_4_out, n3_bit_decoder_1_out3, in_5);
  and and_5 (and_5_out, n3_bit_decoder_1_out4, in_6);
  and and_6 (and_6_out, n3_bit_decoder_1_out5, in_7);
  and and_7 (and_7_out, n3_bit_decoder_1_out6, in_8);
  and and_8 (and_8_out, n3_bit_decoder_1_out7, in_9);
  or or_1 (or_1_out, and_1_out, and_2_out, and_3_out, and_4_out);
  or or_2 (or_2_out, and_5_out, and_6_out, and_7_out, and_8_out);
  or or_3 (out_10, or_1_out, or_2_out);
endmodule
