// Logisim project cache.circ as structural Verilog: 2 circuits, main circuit cache-entry
module main (
  input  [7:0] address,
  input  read_enable,
  input  [31:0] ROM_data_in,
  output [7:0] data_out,
  output [5:0] ROM_read_address,
  output ROM_read_enable
);

  wire cache_entry_1_miss, cache_entry_2_miss, cache_entry_3_miss, cache_entry_4_miss, demultiplexer_2_out0,
       demultiplexer_2_out1, demultiplexer_2_out2, demultiplexer_2_out3, multiplexer_2_out;
  wire [31:0] cache_entry_1_data_out, cache_entry_2_data_out, cache_entry_3_data_out, cache_entry_4_data_out,
       demultiplexer_1_out0, demultiplexer_1_out1, demultiplexer_1_out2, demultiplexer_1_out3,
       multiplexer_1_out;

  Demultiplexer #(.select(2), .width(32), .enable("false")) demultiplexer_1 (
    .out0(demultiplexer_1_out0), .out1(demultiplexer_1_out1), .out2(demultiplexer_1_out2),
    .out3(demultiplexer_1_out3), .in(ROM_data_in), .sel(address[3:2]));
  cache_entry cache_entry_1 (
    .tag(address[7:4]), .clock(demultiplexer_2_out0), .data_out(cache_entry_1_data_out),
    .miss(cache_entry_1_miss), .data_in(demultiplexer_1_out0));
  cache_entry cache_entry_2 (
    .tag(address[7:4]), .clock(demultiplexer_2_out1), .data_out(cache_entry_2_data_out),
    .miss(cache_entry_2_miss), .data_in(demultiplexer_1_out1));
  cache_entry cache_entry_3 (
    .tag(address[7:4]), .clock(demultiplexer_2_out2), .data_out(cache_entry_3_data_out),
    .miss(cache_entry_3_miss), .data_in(demultiplexer_1_out2));
  cache_entry cache_entry_4 (
    .tag(address[7:4]), .clock(demultiplexer_2_out3), .data_out(cache_entry_4_data_out),
    .miss(cache_entry_4_miss), .data_in(demultiplexer_1_out3));
  Multiplexer #(.select(2), .width(32), .enable("false")) multiplexer_1 (
    .in0(cache_entry_1_data_out), .in1(cache_entry_2_data_out), .in2(cache_entry_3_data_out),
    .in3(cache_entry_4_data_out), .out(multiplexer_1_out), .sel(address[3:2]));
  Multiplexer #(.select(2), .enable("false")) multiplexer_2 (
    .in0(cache_entry_1_miss), .in1(cache_entry_2_miss), .in2(cache_entry_3_miss), .in3(cache_entry_4_miss),
    .out(multiplexer_2_out), .sel(address[3:2]));
  Multiplexer #(.select(2), .width(8), .enable("false")) multiplexer_3 (
    .in0(multiplexer_1_out[7:0]), .in1(multiplexer_1_out[15:8]), .in2(multiplexer_1_out[23:16]),
    .in3(multiplexer_1_out[31:24]), .out(data_out), .sel(address[1:0]));
  Demultiplexer #(.select(2), .enable("false")) demultiplexer_2 (
    .out0(demultiplexer_2_out0), .out1(demultiplexer_2_out1), .out2(demultiplexer_2_out2),
    .out3(demultiplexer_2_out3), .in(ROM_read_enable), .sel(address[3:2]));
  and and_1 (ROM_read_enable, read_enable, multiplexer_2_out);

  assign ROM_read_address = address[7:2];

  // Notes on the sheet:
  //   ROM_read_enable: pull=down
  //   ROM_read_address: pull=down
  //   data_out: pull=down
endmodule

module cache_entry (
  input  [31:0] data_in,
  input  [3:0] tag,
  input  clock,
  output [31:0] data_out,
  output miss
);

  wire comparator_1_eq, Valid_Bit_q;
  wire [3:0] Tag_q;

  Register #(.width(32), .trigger("falling")) Cached_Data (
    .D(data_in), .en(miss), .Q(data_out), .clk(clock));  // open: clr
  Register #(.width(4), .trigger("falling")) u_Tag (.D(tag), .en(miss), .Q(Tag_q), .clk(clock));  // open: clr
  Register #(.width(1), .trigger("falling")) Valid_Bit (.D(1'b1), .Q(Valid_Bit_q), .clk(clock));  // open: en, clr
  Comparator #(.width(4)) comparator_1 (.a(tag), .b(Tag_q), .eq(comparator_1_eq));  // open: gt, lt
  nand nand_1 (miss, comparator_1_eq, Valid_Bit_q);
endmodule
